# Fritzing sketch todo_sampleDiagram (saved by Fritzing 0.9.0b)

parts:
  Intel(R)_Galileo_1 = Intel(R) Galileo
  S2 = Toggle Switch [package=THT]
  Part1 = Thermal Printer  # not connected
  X1 = DB9 Connector [package=db9]  # not connected
  X2 = DB9 Connector [package=db9]  # not connected

nets:
  N1: Intel(R)_Galileo_1.D2, S2.L2
  N2: Intel(R)_Galileo_1.5V, S2.L1
  N3: Intel(R)_Galileo_1.GND, S2.COM

custom parts:
  Intel(R) Galileo: Galileo is a microcontroller board based on the Intel® Quark SoC X1000 Application Processor, a 32-bit Intel Pentium-class system on a chip (datasheet). It’s the first board based on Intel® architecture designed to be hardware and software pin-compatible with Arduino shields designed for the Uno R3. Digital pins 0 to 13 (and the adjacent AREF and GND pins), Analog inputs 0 to 5, the power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
